// Logisim project Address_Logic_Improved.circ as structural Verilog: 1 circuit, main circuit main
module main (
  input  A23,
  input  A22,
  input  A21,
  input  A20,
  input  nLDS,
  input  nUDS,
  input  RW,
  output nRAM_ENA,
  output nOE_BANK0,
  output nOE_BANK1,
  output nWE_BANK0,
  output nWE_BANK1,
  output nCS_COL0,
  output nCS_COL1
);

  wire decoder_1_out0, decoder_1_out1, nand_1_out, nOE_out, not_1_out, nRW_out, nWE_out, or_1_out, or_2_out;

  or or_1 (or_1_out, A23, A22);
  or or_2 (or_2_out, A21, A20);
  nand nand_1 (nand_1_out, or_1_out, or_1_out);
  nand nRW (nRW_out, RW, RW);
  nand nand_2 (nRAM_ENA, nand_1_out, or_2_out);
  not not_1 (not_1_out, nRAM_ENA);
  Decoder decoder_1 (.out0(decoder_1_out0), .out1(decoder_1_out1), .sel(A21), .en(not_1_out));
  not not_2 (nCS_COL0, decoder_1_out0);
  not not_3 (nCS_COL1, decoder_1_out1);
  or nOE (nOE_out, nRAM_ENA, RW);
  or nWE (nWE_out, nRAM_ENA, nRW_out);
  or or_3 (nOE_BANK0, nOE_out, nLDS);
  or or_4 (nOE_BANK1, nOE_out, nUDS);
  or or_5 (nWE_BANK0, nWE_out, nLDS);
  or or_6 (nWE_BANK1, nWE_out, nUDS);

  // Notes on the sheet:
  //   ADDR_DIS
  //   ADDR_ENA
  //   nADDR_DIS
  //   NOT gates are part of decoder
endmodule
